// Logisim project AC_1617v_LI21N_Trab1_original.circ as structural Verilog: 4 circuits, main circuit CPU
module CPU (
);

  wire C, EP, ER, MCLK_out, not_1_out, not_2_out, or_1_out, RD, Reset_out, SA, SC, SI, SO, WR;
  wire [0:0] PSW_q;
  wire [1:0] alu_1_z, OP_ALU, SD;
  wire [2:0] AA, AB, AD;
  wire [7:0] adder_1_out, alu_1_r, Const3, Const6, controlled_buffer_1_out, Direct6, multiplexer_1_out,
       multiplexer_2_out, multiplexer_3_out, multiplexer_4_out, multiplexer_5_out, Offset6, PC_q,
       register_file_1_a, register_file_1_b, register_file_1_r0, register_file_1_r1, register_file_1_r2,
       register_file_1_r3, register_file_1_r4, register_file_1_r5, register_file_1_r6, register_file_1_r7;
  wire [12:0] rom_1_data;

  // Probe on Offset6
  Button Reset (.out(Reset_out));
  Clock MCLK (.out(MCLK_out));
  Multiplexer #(.width(8), .enable("false")) multiplexer_1 (
    .in0(8'h1), .in1(Offset6), .out(multiplexer_1_out), .sel(SO));
  Adder adder_1 (.a(multiplexer_1_out), .b(PC_q), .out(adder_1_out), .cin(1'b0));  // open: cout
  Multiplexer #(.width(8), .disabled(0), .enable("false")) multiplexer_2 (
    .in0(adder_1_out), .in1(register_file_1_a), .out(multiplexer_2_out), .sel(SI));
  // Probe on multiplexer_2_out
  // Probe on register_file_1_a
  Register PC (.D(multiplexer_2_out), .en(1'b1), .Q(PC_q), .clk(MCLK_out), .clr(Reset_out));
  not not_1 (not_1_out, MCLK_out);
  // Probe on rom_1_data
  ROM #(.dataWidth(13)) rom_1 (.addr(PC_q), .data(rom_1_data));  // open: sel
  instruction_decode instruction_decode_1 (
    .instructionCode(rom_1_data), .Direct6(Direct6), .Const6(Const6), .Const3(Const3), .Offset8(Offset6),
    .OP_ALU(OP_ALU), .Z(PSW_q[0]), .C(C), .RD(RD), .WR(WR), .EP(EP), .ER(ER), .SA(SA), .SC(SC), .SD(SD),
    .SO(SO), .SI(SI), .AA(AA), .AB(AB), .AD(AD));
  // Probe on SD
  Multiplexer #(.select(2), .width(8), .disabled(0), .enable("false")) multiplexer_3 (
    .in0(Const6), .in1(controlled_buffer_1_out), .in2(alu_1_r), .out(multiplexer_3_out), .sel(SD));  // open: in3
  register_file register_file_1 (
    .AD(AD), .ER(ER), .AA(AA), .AB(AB), .clk(not_1_out), .D(multiplexer_3_out), .A(register_file_1_a),
    .B(register_file_1_b), .R0(register_file_1_r0), .R1(register_file_1_r1), .R2(register_file_1_r2),
    .R3(register_file_1_r3), .R4(register_file_1_r4), .R5(register_file_1_r5), .R6(register_file_1_r6),
    .R7(register_file_1_r7));
  Multiplexer #(.width(8), .enable("false")) multiplexer_4 (
    .in0(Const3), .in1(register_file_1_b), .out(multiplexer_4_out), .sel(SC));
  ALU alu_1 (
    .Ci(1'b0), .A(register_file_1_a), .B(multiplexer_4_out), .Co(alu_1_z[1]), .Z(alu_1_z[0]), .R(alu_1_r),
    .OP_ALU(OP_ALU));
  // Probe on register_file_1_r0
  // Probe on register_file_1_r1
  // Probe on register_file_1_r2
  // Probe on register_file_1_r3
  // Probe on register_file_1_r4
  // Probe on register_file_1_r5
  // Probe on alu_1_r
  // Probe on register_file_1_r6
  // Probe on register_file_1_r7
  Multiplexer #(.width(8), .enable("false")) multiplexer_5 (
    .in0(Direct6), .in1(register_file_1_b), .out(multiplexer_5_out), .sel(SA));
  // Probe on multiplexer_5_out
  // Probe on controlled_buffer_1_out
  assign controlled_buffer_1_out = WR ? register_file_1_a : 8'bz;  // Controlled_Buffer controlled_buffer_1
  Register #(.width(2)) PSW (.D(alu_1_z), .en(EP), .Q({C, PSW_q[0]}), .clk(not_1_out));  // open: clr
  // Probe on {C, PSW_q[0]}
  not not_2 (not_2_out, WR);
  or or_1 (or_1_out, WR, RD);
  RAM ram_1 (
    .addr(multiplexer_5_out), .data(controlled_buffer_1_out), .sel(or_1_out), .clk(not_1_out),
    .ld(not_2_out), .clr(1'b0));

  // Notes on the sheet:
  //   Code memory
  //   contents of rom_1 (hex, n*v repeats v):
  //   1004 649 1280 4a 201 1a3d 1014 1608 1e00
  //   Data memory
endmodule

module register_file (
  input  [7:0] D,
  input  [2:0] AD,
  input  ER,
  input  [2:0] AA,
  input  [2:0] AB,
  input  clk,
  output [7:0] R0,
  output [7:0] R1,
  output [7:0] R2,
  output [7:0] R3,
  output [7:0] R4,
  output [7:0] R5,
  output [7:0] R6,
  output [7:0] R7,
  output [7:0] A,
  output [7:0] B
);

  wire decoder_1_out0, decoder_1_out1, decoder_1_out2, decoder_1_out3, decoder_1_out4, decoder_1_out5,
       decoder_1_out6, decoder_1_out7;

  Decoder #(.select(3), .disabled(0)) decoder_1 (
    .out0(decoder_1_out0), .out1(decoder_1_out1), .out2(decoder_1_out2), .out3(decoder_1_out3),
    .out4(decoder_1_out4), .out5(decoder_1_out5), .out6(decoder_1_out6), .out7(decoder_1_out7), .sel(AD),
    .en(ER));
  Register u_R0 (.D(D), .en(decoder_1_out0), .Q(R0), .clk(clk));  // open: clr
  Multiplexer #(.select(3), .width(8), .disabled(0), .enable("false")) multiplexer_1 (
    .in0(R0), .in1(R1), .in2(R2), .in3(R3), .in4(R4), .in5(R5), .in6(R6), .in7(R7), .out(A), .sel(AA));
  Register u_R1 (.D(D), .en(decoder_1_out1), .Q(R1), .clk(clk));  // open: clr
  Register u_R2 (.D(D), .en(decoder_1_out2), .Q(R2), .clk(clk));  // open: clr
  Multiplexer #(.select(3), .width(8), .disabled(0), .enable("false")) multiplexer_2 (
    .in0(R0), .in1(R1), .in2(R2), .in3(R3), .in4(R4), .in5(R5), .in6(R6), .in7(R7), .out(B), .sel(AB));
  Register u_R3 (.D(D), .en(decoder_1_out3), .Q(R3), .clk(clk));  // open: clr
  Register u_R4 (.D(D), .en(decoder_1_out4), .Q(R4), .clk(clk));  // open: clr
  Register u_R5 (.D(D), .en(decoder_1_out5), .Q(R5), .clk(clk));  // open: clr
  Register u_R6 (.D(D), .en(decoder_1_out6), .Q(R6), .clk(clk));  // open: clr
  Register u_R7 (.D(D), .en(decoder_1_out7), .Q(R7), .clk(clk));  // open: clr
endmodule

module instruction_decode (
  input  [12:0] instructionCode,
  input  C,
  input  Z,
  output [2:0] AB,
  output [2:0] AA,
  output [2:0] AD,
  output [7:0] Direct6,
  output [7:0] Const6,
  output [7:0] Const3,
  output [7:0] Offset8,
  output [1:0] OP_ALU,
  output RD,
  output WR,
  output EP,
  output ER,
  output SA,
  output SC,
  output [1:0] SD,
  output SO,
  output SI
);

  ROM #(.addrWidth(6), .dataWidth(10)) rom_1 (
    .addr({instructionCode[12:9], Z, C}), .data({SI, SO, SD, SC, SA, ER, EP, WR, RD}));  // open: sel

  assign AA = instructionCode[5:3];
  assign AB = instructionCode[2:0];
  assign AD = instructionCode[8:6];
  assign Const3 = {{5{1'b0}}, instructionCode[2:0]};
  assign Const6 = {2'b00, instructionCode[5:0]};
  assign Direct6 = {2'b00, instructionCode[5:0]};
  assign Offset8 = {{3{instructionCode[5]}}, instructionCode[4:0]};
  assign OP_ALU = instructionCode[10:9];

  // Notes on the sheet:
  //   contents of rom_1 (hex, n*v repeats v):
  //   4*ac 4*8c 8*ac 16*0 4*8 4*59 4*49 4*12 0 0 100 100 100 0 100 0 4*100 4*200
endmodule

module ALU (
  input  Ci,
  input  [7:0] A,
  input  [7:0] B,
  input  [1:0] OP_ALU,
  output Co,
  output Z,
  output [7:0] R
);

  wire adder_1_cout, xor_1_out;
  wire [7:0] adder_1_out, and_1_out, bit_extender_1_out, multiplexer_1_out, xor_2_out, xor_3_out;

  assign bit_extender_1_out = {{7{OP_ALU[0]}}, OP_ALU[0]};  // Bit_Extender bit_extender_1
  xor xor_1 (xor_1_out, Ci, OP_ALU[0]);
  assign xor_2_out = B ^ bit_extender_1_out;  // XOR_Gate xor_2, 8 bits wide
  Adder adder_1 (.a(A), .b(xor_2_out), .out(adder_1_out), .cin(xor_1_out), .cout(adder_1_cout));
  assign and_1_out = A & B;  // AND_Gate and_1, 8 bits wide
  assign xor_3_out = B ^ A;  // XOR_Gate xor_3, 8 bits wide
  xor xor_4 (Co, adder_1_cout, OP_ALU[0]);
  Multiplexer #(.width(8), .enable("false")) multiplexer_1 (
    .in0(and_1_out), .in1(xor_3_out), .out(multiplexer_1_out), .sel(OP_ALU[0]));
  Multiplexer #(.width(8), .enable("false")) multiplexer_2 (
    .in0(adder_1_out), .in1(multiplexer_1_out), .out(R), .sel(OP_ALU[1]));
  and and_2 (Z, ~R[0], ~R[1], ~R[2], ~R[3], ~R[4], ~R[5], ~R[6], ~R[7]);  // AND_Gate
endmodule
